// Logisim project 2_Boolean_Arithmetic.circ as structural Verilog: 1 circuit, main circuit main
module main (
  input  a,
  input  b,
  input  a_2,
  input  b_2,
  input  cin,
  input  a_3,
  input  in_7,
  input  in_8,
  input  in_9,
  input  in_10,
  input  in_11,
  input  in_12,
  input  in_13,
  input  in_14,
  input  in_15,
  input  in_16,
  input  in_17,
  input  in_18,
  input  in_19,
  input  in_20,
  input  in_21,
  output sum,
  output carry,
  output sum1,
  output sum_2,
  output cout
);

  wire and_1_out, and_3_out;

  xor xor_1 (sum1, a_2, b_2);
  and and_1 (and_1_out, a_2, b_2);
  xor xor_2 (sum, a, b);
  and and_2 (carry, a, b);
  xor xor_3 (sum_2, sum1, cin);
  and and_3 (and_3_out, sum1, cin);
  or or_1 (cout, and_1_out, and_3_out);

  // Notes on the sheet:
  //   Input
  //   Input
  //   Input
  //   Bitwise XOR
  //   Bitwise AND
  //   Bitwise XOR
  //   Bitwise AND
  //   Bitwise XOR
  //   Bitwise AND
  //   Output
  //   carry1
  //   carry2
  //   Output
endmodule
